# Fritzing sketch ExoLab V1 (saved by Fritzing 1.0.5)
perfboards: 1

parts:
  LED1 = LED - 5mm [color="Red (633nm)" current=0.030A package="5 mm [THT]"]
  Power_plug1 = Power plug
  R1 = Resistor [tolerance=±5% power=0.25W resistance=220 package=THT]
  C1 = Electrolytic Capacitor [capacitance=1µF voltage=35V package="100 mil [THT, electrolytic]"]
  Part1 = Adafruit APDS-9960 [part_number="Adafruit #3595"]  # not connected
  Part2 = OLED Monochrome 128x32 I2C [part_number=931]  # not connected
  Part4 = Adafruit SCD4x [part_number="Adafruit #5187"]  # not connected
  Raspberry_Pi_1 = Raspberry Pi 3 [part_number=RPI-3-V1.2]  # not connected
  IC1 = Rasberry Pi NIOR Camera [chip_label=IC package="DIP (Dual Inline) [THT]"]  # not connected

nets:
  N1: LED1.cathode, R1.Pin_1
  N2: Power_plug1.VCC, C1.+

notes:
  To LED Panel DIO Input
  To LED Panel Positive
  To LED Panel Negative
  Fish-eye camera connected to camera input
  These devices connected via Adafruit STEMMA QT / Qwiic JST cables
  NOTE: LED Panel GND must also be connected to RPi GND
  NOTE: In theory, this power supply should also be able to power the RPi, but RPi would report low power.
  NOTE: Need to power RPi via USB

custom parts:
  Adafruit APDS-9960: The APDS9960 from Avago Technologies has an integrated IR LED and driver, along with four directional photodiodes that sense reflected IR energy from the LED. It's proximity detection feature allows it to measure the distance an object is from the front of the sensor (up to a few centimeters) with 8 bit resolution. Since there are four IR sensors, you can measure the changes in light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
  OLED Monochrome 128x32 I2C: These displays are small, only about 1" diagonal, but very readable due to the high contrast of an OLED display. This display is made of 128x32 individual white OLED pixels, each one is turned on or off by the controller chip. Because the display makes its own light, no backlight is required. This reduces the power required to run the OLED and is why the display has such high contrast; we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
  Adafruit SCD4x: Take a deep breath in...now slowly breathe out. Mmm isn't it wonderful? All that air around us, which we bring into our lungs, extracts oxygen from and then breathes out carbon dioxide. CO2 is essential for life on this planet we call Earth - we and plants take turns using and emitting CO2 in an elegant symbiosis. But it's important to keep that CO2 balanced - you don't want too much around,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
  Rasberry Pi NIOR Camera: Camera
